# Fritzing sketch Baby Ambient Room Temperature Monitor (saved by Fritzing 0.9.3b)

parts:
  Part1 = Arduino Pro Mini (5V)
  RGB_LED = RGB LED - (4 legs) [package="5 mm [THT]"]
  R1 = Resistor [tolerance=±0.5% resistance=100 package=THT]
  R2 = Resistor [tolerance=±0.5% resistance=100 package=THT]
  R3 = Resistor [tolerance=±0.5% resistance=150 package=THT]
  R4 = Photocell (LDR) [package=THT]
  R5 = Resistor [tolerance=±0.5% resistance=10k package=THT]
  T1 = LM35 Temperature Sensor [part_number=LM335z package="TO92 [THT]"]
  R6 = Resistor [tolerance=±0.5% resistance=2.2k package=THT]

nets:
  GND: Part1.GND, R5.Pin_1, T1.GND
  N1: Part1.VCC, R6.Pin_0
  N2: Part1.A3, R4.pin_1, R5.Pin_0
  N3: Part1.A0, T1.Vout, R6.Pin_1
  N4: Part1.D9, R3.Pin_1
  N5: Part1.D8, RGB_LED.common_anode
  N6: Part1.D6, R1.Pin_1
  N7: Part1.D5, R2.Pin_1
  N8: Part1.D2, R4.pin_0
  N9: RGB_LED.red_cathode, R3.Pin_0
  N10: RGB_LED.green_cathode, R1.Pin_0
  N11: RGB_LED.blue_cathode, R2.Pin_0
